# Fritzing sketch sketch (saved by Fritzing 0.9.3b)
breadboards: 1

parts:
  Part1 = Arduino Uno (Rev3)
  M1 = Dagu DGServo 9g (Top view) [part_number=RS001B]
  Part2 = RFID-RC522-v2

nets:
  N1: Part1.D9_PWM, Part2.RST
  N2: Part1.D10_PWM/SS, Part2.SDA
  N3: Part1.D11_PWM/MOSI, Part2.MOSI
  N4: Part1.D12/MISO, Part2.MISO
  N5: Part1.D13/SCK, Part2.SCK
  N6: Part1.D7, M1.pulse
  3V3: Part1.3V3, Part2.3.3V
  5V: Part1.5V, M1.vcc
  GND: Part1.GND, M1.gnd, Part2.GND

custom parts:
  RFID-RC522-v2: A simple China made RFID-RC522 Reader; do check the pin labels, as this is a MFRC522 based clone.
